# Fritzing sketch prtable_gimbal (saved by Fritzing 0.9.3b)
breadboards: 1

parts:
  J1 = Basic Servo
  J2 = Basic Servo
  Part1 = Arduino Uno (Rev3) - ICSP
  VCC4 = Battery block 9V
  VCC5 = Battery block 9V
  VCC3 = 4 x AAA Battery Mount
  GY2 = MPU-6050 Board GY-521 [form="♀ (female)" package=THT]

nets:
  GND: J1.gnd, J2.gnd, Part1.GND, VCC4.-, VCC5.-, VCC3.-, GY2.pin2
  VCC: J1.vcc, J2.vcc, VCC3.+
  N1: J1.pulse, Part1.D5_PWM
  N2: J2.pulse, Part1.D9_PWM
  N3: Part1.A4/SDA, GY2.pin4
  N4: Part1.A5/SCL, GY2.pin3
  N5: Part1.5V, GY2.pin1
  N6: Part1.VIN, VCC4.+, VCC5.+

custom parts:
  MPU-6050 Board GY-521: Acelerometro y Giroscopio MPU-6050 Board GY-521
