# Fritzing sketch wire (saved by Fritzing 0.9.3b)
breadboards: 1

parts:
  Part2 = Arduino Uno (Rev3) - ICSP
  GY3 = MPU-6050 Board GY-521 [form="♀ (female)" package=THT]
  J1 = Basic Servo
  J2 = Basic Servo
  VCC1 = 4 x AAA Battery Mount

nets:
  N1: Part2.A4/SDA, GY3.pin4
  N2: Part2.A5/SCL, GY3.pin3
  N3: Part2.D9_PWM, J2.pulse
  GND: Part2.GND, GY3.pin2, J1.gnd, J2.gnd, VCC1.-
  N4: Part2.D5_PWM, J1.pulse
  N5: Part2.5V, GY3.pin1
  VCC: J1.vcc, J2.vcc, VCC1.+

custom parts:
  MPU-6050 Board GY-521: Acelerometro y Giroscopio MPU-6050 Board GY-521
